// Logisim project jrmips.circ as structural Verilog: 15 circuits, main circuit main
module main (
);

  wire B_Logic, branch_type_1_condition_0, branch_type_1_condition_1, branch_type_1_is_branch, CLK,
       comparator_1_eq, comparator_1_gt, comparator_1_lt, halt_check_1_halt, I_or_J, j_logic, jal_logic,
       jr_logic, put_check_1_put, Subop, write_control_1_write;
  wire [1:0] alu_op_1_alu_instr1, data_mem_control_1_data_0, multiplexer_10_out, Reg_Ctrl;
  wire [2:0] RS;
  wire [3:0] multiplexer_8_out, Opcode;
  wire [7:0] _8_bit_rs, Imm, multiplexer_1_out, multiplexer_2_out, multiplexer_3_out, multiplexer_4_out,
       PC_1, register_1_q;
  wire [15:0] ALU_DATA, bit_extender_1_out, bit_extender_2_out, bit_extender_3_out, mem_data,
       multiplexer_5_out, multiplexer_6_out, multiplexer_7_out, register_2_q, RS_Data, RT_Data,
       Shift_Logical_Data, shifter_1_out, shifter_2_out;

  Clock clock_1 (.out(CLK));
  Multiplexer #(.width(8)) multiplexer_1 (
    .in0(multiplexer_2_out), .in1(Imm), .out(multiplexer_1_out), .sel(jal_logic));  // open: en
  Adder adder_1 (.a(8'h1), .b(register_1_q), .out(PC_1));  // open: cin, cout
  Register register_1 (.D(multiplexer_1_out), .en(halt_check_1_halt), .Q(register_1_q), .clk(CLK));  // open: clr
  DotMatrix #(.matrixcols(1), .matrixrows(1)) dotmatrix_1 (.col0(halt_check_1_halt));
  Multiplexer #(.width(8)) multiplexer_2 (
    .in0(multiplexer_4_out), .in1(Imm), .out(multiplexer_2_out), .sel(j_logic));  // open: en
  Multiplexer #(.width(8)) multiplexer_3 (.in0(PC_1), .in1(Imm), .out(multiplexer_3_out), .sel(B_Logic));  // open: en
  Halt_Check halt_check_1 (
    .Opcode_0(Opcode[0]), .Opcode_1(Opcode[1]), .Opcode_2(Opcode[2]), .Opcode_3(Opcode[3]),
    .Halt(halt_check_1_halt));
  Multiplexer #(.width(8)) multiplexer_4 (
    .in0(multiplexer_3_out), .in1(_8_bit_rs), .out(multiplexer_4_out), .sel(jr_logic));  // open: en
  ROM #(.dataWidth(16)) rom_1 (.addr(register_1_q), .data({Opcode, RS, Imm, Subop}));  // open: sel
  JAL_Logic jal_logic_1 (
    .Opcode_3(Opcode[3]), .Opcode_2(Opcode[2]), .Opcode_1(Opcode[1]), .Opcode_0(Opcode[0]), .Subop(Subop),
    .pc_to_rs(jal_logic));
  R_I_Decoder r_i_decoder_1 (
    .Opcode_0(Opcode[3]), .Opcode_1(Opcode[2]), .Opcode_2(Opcode[1]), .Opcode_3(Opcode[0]), .Subop(Subop),
    .Format(I_or_J));
  Reg_Control reg_control_1 (
    .Opcode_3(Opcode[3]), .Opcode_2(Opcode[2]), .Opcode_1(Opcode[1]), .Opcode_0(Opcode[0]), .Subop(Subop),
    .Data_0(Reg_Ctrl[1]), .Data_1(Reg_Ctrl[0]));
  JR_Logic jr_logic_1 (
    .Opcode_3(Opcode[3]), .Opcode_2(Opcode[2]), .Opcode_1(Opcode[1]), .Opcode_0(Opcode[0]), .Subop(Subop),
    .pc_to_rs(jr_logic));
  BitSelector #(.width(16), .group(8)) bitselector_1 (.in(RS_Data), .out(_8_bit_rs), .sel(1'b0));
  Write_Control write_control_1 (
    .Opcode_3(Opcode[3]), .Opcode_2(Opcode[2]), .Opcode_1(Opcode[1]), .Opcode_0(Opcode[0]), .Subop(Subop),
    .Write(write_control_1_write));
  assign bit_extender_1_out = {{8{1'b0}}, PC_1};  // Bit_Extender bit_extender_1
  Multiplexer #(.select(2), .width(16)) multiplexer_5 (
    .in0(ALU_DATA), .in1(Shift_Logical_Data), .in2(mem_data), .in3(bit_extender_1_out),
    .out(multiplexer_5_out), .sel(Reg_Ctrl));  // open: en
  Register_File register_file_1 (
    .ReadRegister1(RS), .ReadRegister2(Imm[7:5]), .WriteRegister(RS), .WriteData(multiplexer_5_out),
    .Clock(CLK), .Write_Enable(write_control_1_write), .ReadData1(RS_Data), .ReadData2(RT_Data));
  assign bit_extender_2_out = {{8{1'b0}}, Imm};  // Bit_Extender bit_extender_2
  assign bit_extender_3_out = {{8{Imm[7]}}, Imm};  // Bit_Extender bit_extender_3
  J_Logic j_logic_1 (
    .Opcode_3(Opcode[3]), .Opcode_2(Opcode[2]), .Opcode_1(Opcode[1]), .Opcode_0(Opcode[0]), .Subop(Subop),
    .pc_to_rs(j_logic));
  Multiplexer #(.width(16)) multiplexer_6 (
    .in0(bit_extender_2_out), .in1(bit_extender_3_out), .out(multiplexer_6_out), .sel(Subop));  // open: en
  Multiplexer #(.width(16)) multiplexer_7 (
    .in0(RT_Data), .in1(multiplexer_6_out), .out(multiplexer_7_out), .sel(I_or_J));  // open: en
  ALU alu_1 (.Input_1(RS_Data), .Input_2(multiplexer_7_out), .Opcode(alu_op_1_alu_instr1), .ALU_Result(ALU_DATA));
  ALU_OP alu_op_1 (
    .Opcode_0(Opcode[0]), .Opcode_1(Opcode[1]), .Opcode_2(Opcode[2]), .Opcode_3(Opcode[3]),
    .ALU_instr0(alu_op_1_alu_instr1[1]), .ALU_instr1(alu_op_1_alu_instr1[0]));
  Put_Check put_check_1 (
    .Opcode_0(Opcode[0]), .Opcode_1(Opcode[1]), .Opcode_2(Opcode[2]), .Opcode_3(Opcode[3]),
    .Put(put_check_1_put));
  Multiplexer #(.width(4)) multiplexer_8 (
    .in0(Imm[3:0]), .in1(RT_Data[3:0]), .out(multiplexer_8_out), .sel(Subop));  // open: en
  Register #(.width(16)) register_2 (.D(RS_Data), .en(put_check_1_put), .Q(register_2_q), .clk(CLK));  // open: clr
  Shifter #(.width(16)) shifter_1 (.in(RS_Data), .\dist (multiplexer_8_out), .out(shifter_1_out));
  Shifter #(.width(16), .shift("lr")) shifter_2 (.in(RS_Data), .\dist (multiplexer_8_out), .out(shifter_2_out));
  Hex_Digit_Display hex_digit_display_1 (.value(register_2_q[15:12]));  // open: dp
  Multiplexer #(.width(16)) multiplexer_9 (
    .in0(shifter_1_out), .in1(shifter_2_out), .out(Shift_Logical_Data), .sel(Opcode[0]));  // open: en
  Hex_Digit_Display hex_digit_display_2 (.value(register_2_q[11:8]));  // open: dp
  Hex_Digit_Display hex_digit_display_3 (.value(register_2_q[7:4]));  // open: dp
  Data_mem_control data_mem_control_1 (
    .Opcode_3(Opcode[3]), .Opcode_2(Opcode[2]), .Opcode_1(Opcode[1]), .Opcode_0(Opcode[0]), .Subop(Subop),
    .Data_0(data_mem_control_1_data_0[0]), .Data_1(data_mem_control_1_data_0[1]));
  Hex_Digit_Display hex_digit_display_4 (.value(register_2_q[3:0]));  // open: dp
  Multiplexer #(.select(2), .width(2)) multiplexer_10 (
    .in0(2'b00), .in1(2'b01), .in2(2'b10), .out(multiplexer_10_out), .sel(data_mem_control_1_data_0));  // open: in3, en
  RAM #(.dataWidth(16), .bus("separate")) ram_1 (
    .addr(RT_Data[7:0]), .din(RS_Data), .data(mem_data), .str(multiplexer_10_out[0]), .clk(CLK),
    .ld(multiplexer_10_out[1]));  // open: sel, clr
  Branch_Type branch_type_1 (
    .Opcode_3(Opcode[3]), .Opcode_2(Opcode[2]), .Opcode_1(Opcode[1]), .Opcode_0(Opcode[0]), .Subop(Subop),
    .is_branch(branch_type_1_is_branch), .condition_0(branch_type_1_condition_0),
    .condition_1(branch_type_1_condition_1));
  Comparator #(.width(16)) comparator_1 (
    .a(RS_Data), .b({16{1'b0}}), .gt(comparator_1_gt), .eq(comparator_1_eq), .lt(comparator_1_lt));
  Branch_Logic branch_logic_1 (
    .Branch_2(branch_type_1_is_branch), .Branch_1(branch_type_1_condition_0),
    .Branch_0(branch_type_1_condition_1), .Compare_2(comparator_1_gt), .Compare_1(comparator_1_eq),
    .Compare_0(comparator_1_lt), .change_PC_to_imm(B_Logic));

  // Other names for the same wires on the sheet: Shamt[3:0] = Imm[3:0]; RT[2:0] = Imm[7:5]

  // Notes on the sheet:
  //   Processor Status(Green = ON, Red = OFF)
  //   Program Counter
  //   Instruction Memory
  //   Halt_check
  //   Instruction Separator
  //   jal_logic
  //   Shamt
  //   Imm
  //   RT
  //   R_I_Decoder
  //   RS
  //   Opcode
  //   jr_logic
  //   Register Control
  //   Alessio Mazzone  ALM238@pitt.edu   0447     Childers MW 3-415      Assignment 3     jrMIPS Processor
  //   Write Control
  //   Register File
  //   j_logic
  //   ALU
  //   Put_Check
  //   Shift Logic
  //   Data Memory
  //   Branch Logic
endmodule

module ALU (
  input  [15:0] Input_1,
  input  [15:0] Input_2,
  input  [1:0] Opcode,
  output [15:0] ALU_Result
);

  wire [15:0] adder_1_out, and_1_out, nor_1_out, subtractor_1_out;

  Adder #(.width(16)) adder_1 (.a(Input_1), .b(Input_2), .out(adder_1_out));  // open: cin, cout
  assign and_1_out = Input_1 & Input_2;  // AND_Gate and_1, 16 bits wide
  assign nor_1_out = ~(Input_1 | Input_2);  // NOR_Gate nor_1, 16 bits wide
  Subtractor #(.width(16)) subtractor_1 (.a(Input_1), .b(Input_2), .out(subtractor_1_out));  // open: bin, bout
  Multiplexer #(.select(2), .width(16)) multiplexer_1 (
    .in0(and_1_out), .in1(nor_1_out), .in2(adder_1_out), .in3(subtractor_1_out), .out(ALU_Result),
    .sel(Opcode));  // open: en
endmodule

module Register_File (
  input  Write_Enable,
  input  [2:0] ReadRegister1,
  input  [2:0] ReadRegister2,
  input  [2:0] WriteRegister,
  input  [15:0] WriteData,
  input  Clock,
  output [15:0] ReadData1,
  output [15:0] ReadData2
);

  wire demultiplexer_2_out0, demultiplexer_2_out1, demultiplexer_2_out2, demultiplexer_2_out3,
       demultiplexer_2_out4, demultiplexer_2_out5, demultiplexer_2_out6, demultiplexer_2_out7, undriven;
  wire [15:0] demultiplexer_1_out0, demultiplexer_1_out1, demultiplexer_1_out2, demultiplexer_1_out3,
       demultiplexer_1_out4, demultiplexer_1_out5, demultiplexer_1_out6, demultiplexer_1_out7, register_1_q,
       register_2_q, register_3_q, register_4_q, register_5_q, register_6_q, register_7_q, register_8_q;

  Demultiplexer #(.select(3), .width(16)) demultiplexer_1 (
    .out0(demultiplexer_1_out0), .out1(demultiplexer_1_out1), .out2(demultiplexer_1_out2),
    .out3(demultiplexer_1_out3), .out4(demultiplexer_1_out4), .out5(demultiplexer_1_out5),
    .out6(demultiplexer_1_out6), .out7(demultiplexer_1_out7), .in(WriteData), .sel(WriteRegister));  // open: en
  Demultiplexer #(.select(3)) demultiplexer_2 (
    .out0(demultiplexer_2_out0), .out1(demultiplexer_2_out1), .out2(demultiplexer_2_out2),
    .out3(demultiplexer_2_out3), .out4(demultiplexer_2_out4), .out5(demultiplexer_2_out5),
    .out6(demultiplexer_2_out6), .out7(demultiplexer_2_out7), .in(Write_Enable), .sel(WriteRegister));  // open: en
  Register #(.width(16)) register_1 (
    .D(demultiplexer_1_out0), .en(demultiplexer_2_out0), .Q(register_1_q), .clk(Clock));  // open: clr
  Register #(.width(16)) register_2 (
    .D(demultiplexer_1_out1), .en(demultiplexer_2_out1), .Q(register_2_q), .clk(Clock));  // open: clr
  Register #(.width(16)) register_3 (
    .D(demultiplexer_1_out2), .en(demultiplexer_2_out2), .Q(register_3_q), .clk(Clock));  // open: clr
  Register #(.width(16)) register_4 (
    .D(demultiplexer_1_out3), .en(demultiplexer_2_out3), .Q(register_4_q), .clk(Clock));  // open: clr
  Register #(.width(16)) register_5 (
    .D(demultiplexer_1_out4), .en(demultiplexer_2_out4), .Q(register_5_q), .clk(Clock));  // open: clr
  Register #(.width(16)) register_6 (
    .D(demultiplexer_1_out5), .en(demultiplexer_2_out5), .Q(register_6_q), .clk(Clock));  // open: clr
  Register #(.width(16)) register_7 (
    .D(demultiplexer_1_out6), .en(demultiplexer_2_out6), .Q(register_7_q), .clk(Clock));  // open: clr
  Register #(.width(16)) register_8 (
    .D(demultiplexer_1_out7), .en(demultiplexer_2_out7), .Q(register_8_q), .clk(Clock));  // open: clr
  Multiplexer #(.select(3), .width(16)) multiplexer_1 (
    .in0(register_1_q), .in1(register_2_q), .in2(register_3_q), .in3(register_4_q), .in4(register_5_q),
    .in5(register_6_q), .in6(register_7_q), .in7(register_8_q), .out(ReadData1), .sel(ReadRegister1),
    .en(undriven));
  Multiplexer #(.select(3), .width(16)) multiplexer_2 (
    .in0(register_1_q), .in1(register_2_q), .in2(register_3_q), .in3(register_4_q), .in4(register_5_q),
    .in5(register_6_q), .in6(register_7_q), .in7(register_8_q), .out(ReadData2), .sel(ReadRegister2));  // open: en
  ROM #(.dataWidth(16)) rom_1 ();  // open: addr, data, sel

  // Other names for the same wires on the sheet: A[2:0] = ReadRegister1; B[2:0] = ReadRegister2

  // Notes on the sheet:
  //   contents of rom_1 (hex, n*v repeats v):
  //   1 f000 1001 241 200 12f0 b201 10ff 481 1503 5008 f000 14ff a40a 1 1108 5018 901 190f 5818 481 1504
  //   f000 6c1 600 3701 5609 30c0 3000 5809 14ff 8421 8e16 7000
endmodule

module R_I_Decoder (
  input  Opcode_0,
  input  Opcode_1,
  input  Opcode_2,
  input  Opcode_3,
  input  Subop,
  output Format
);

  wire and_1_out, and_2_out, and_3_out, and_4_out, not_1_out, not_2_out, not_3_out, not_4_out, not_5_out,
       not_6_out, not_7_out;

  not not_1 (not_1_out, Opcode_1);
  not not_2 (not_2_out, Opcode_2);
  not not_3 (not_3_out, Opcode_3);
  not not_4 (not_4_out, Opcode_0);
  not not_5 (not_5_out, Opcode_1);
  not not_6 (not_6_out, Opcode_2);
  not not_7 (not_7_out, Opcode_2);
  and and_1 (and_1_out, not_1_out, not_2_out, not_3_out);
  and and_2 (and_2_out, not_4_out, Opcode_2, Opcode_3);
  and and_3 (and_3_out, Opcode_0, not_5_out, not_6_out, Subop);
  and and_4 (and_4_out, Opcode_0, Opcode_1, not_7_out, Opcode_3);
  or or_1 (Format, and_1_out, and_2_out, and_3_out, and_4_out);
endmodule

module ALU_OP (
  input  Opcode_0,
  input  Opcode_1,
  input  Opcode_2,
  input  Opcode_3,
  output ALU_instr0,
  output ALU_instr1
);

  wire not_1_out;

  not not_1 (not_1_out, Opcode_2);
  or or_1 (ALU_instr0, not_1_out, Opcode_3);

  assign ALU_instr1 = Opcode_0;
endmodule

module Put_Check (
  input  Opcode_0,
  input  Opcode_1,
  input  Opcode_2,
  input  Opcode_3,
  output Put
);

  wire not_1_out, not_2_out;

  not not_1 (not_1_out, Opcode_2);
  not not_2 (not_2_out, Opcode_3);
  and and_1 (Put, Opcode_0, Opcode_1, not_1_out, not_2_out);
endmodule

module Halt_Check (
  input  Opcode_0,
  input  Opcode_1,
  input  Opcode_2,
  input  Opcode_3,
  output Halt
);

  wire not_1_out, not_2_out, not_3_out, not_4_out;

  not not_1 (not_1_out, Opcode_0);
  not not_2 (not_2_out, Opcode_1);
  not not_3 (not_3_out, Opcode_2);
  not not_4 (not_4_out, Opcode_3);
  or or_1 (Halt, not_1_out, not_2_out, not_3_out, not_4_out);
endmodule

module Reg_Control (
  input  Opcode_3,
  input  Opcode_2,
  input  Opcode_1,
  input  Opcode_0,
  input  Subop,
  output Data_0,
  output Data_1
);

  wire and_1_out, and_2_out, and_3_out, and_4_out, and_5_out, not_1_out, not_2_out, not_3_out, not_4_out;

  not not_1 (not_1_out, Opcode_2);
  not not_2 (not_2_out, Opcode_1);
  not not_3 (not_3_out, Opcode_1);
  not not_4 (not_4_out, Opcode_1);
  and and_1 (and_1_out, Opcode_2, Opcode_1);
  and and_2 (and_2_out, Opcode_3, not_1_out, not_2_out, Opcode_0, Subop);
  and and_3 (and_3_out, Opcode_2, not_3_out);
  and and_4 (and_4_out, Opcode_3, not_4_out, Opcode_0, Subop);
  and and_5 (and_5_out, Opcode_3, Opcode_2);
  or or_1 (Data_0, and_1_out, and_2_out);
  or or_2 (Data_1, and_3_out, and_4_out, and_5_out);
endmodule

module Data_mem_control (
  input  Opcode_3,
  input  Opcode_2,
  input  Opcode_1,
  input  Opcode_0,
  input  Subop,
  output Data_0,
  output Data_1
);

  wire not_1_out, not_2_out, not_3_out, not_4_out, not_5_out;

  not not_1 (not_1_out, Opcode_3);
  not not_2 (not_2_out, Opcode_0);
  not not_3 (not_3_out, Opcode_3);
  not not_4 (not_4_out, Opcode_0);
  not not_5 (not_5_out, Subop);
  and and_1 (Data_0, not_1_out, Opcode_2, Opcode_1, not_2_out, Subop);
  and and_2 (Data_1, not_3_out, Opcode_2, Opcode_1, not_4_out, not_5_out);
endmodule

module Branch_Type (
  input  Opcode_3,
  input  Opcode_2,
  input  Opcode_1,
  input  Opcode_0,
  input  Subop,
  output is_branch,
  output condition_0,
  output condition_1
);

  wire and_1_out, and_2_out, and_4_out, and_5_out, not_1_out, not_2_out, not_3_out, not_4_out, not_5_out,
       not_6_out, not_7_out, not_8_out, not_9_out, not_10_out, not_11_out;

  not not_1 (not_1_out, Opcode_3);
  not not_2 (not_2_out, Opcode_2);
  not not_3 (not_3_out, Opcode_1);
  not not_4 (not_4_out, Opcode_0);
  not not_5 (not_5_out, Opcode_2);
  not not_6 (not_6_out, Opcode_1);
  not not_7 (not_7_out, Opcode_0);
  not not_8 (not_8_out, Opcode_3);
  not not_9 (not_9_out, Opcode_2);
  not not_10 (not_10_out, Opcode_1);
  not not_11 (not_11_out, Opcode_0);
  and and_1 (and_1_out, not_1_out, Opcode_2, Opcode_1, Opcode_0);
  and and_2 (and_2_out, Opcode_3, not_2_out, not_3_out, not_4_out);
  and and_3 (condition_0, Opcode_3, not_5_out, not_6_out, not_7_out);
  and and_4 (and_4_out, not_8_out, Opcode_2, Opcode_1, Opcode_0, Subop);
  and and_5 (and_5_out, Opcode_3, not_9_out, not_10_out, not_11_out, Subop);
  or or_1 (is_branch, and_1_out, and_2_out);
  or or_2 (condition_1, and_4_out, and_5_out);
endmodule

module Branch_Logic (
  input  Branch_2,
  input  Branch_1,
  input  Branch_0,
  input  Compare_2,
  input  Compare_1,
  input  Compare_0,
  output change_PC_to_imm
);

  wire and_1_out, and_2_out, and_3_out, and_4_out, not_1_out, not_2_out, not_3_out, not_4_out, not_5_out,
       not_6_out, not_7_out, not_8_out, not_9_out, not_10_out, not_11_out, not_12_out;

  not not_1 (not_1_out, Branch_0);
  not not_2 (not_2_out, Compare_2);
  not not_3 (not_3_out, Compare_1);
  not not_4 (not_4_out, Branch_1);
  not not_5 (not_5_out, Branch_0);
  not not_6 (not_6_out, Compare_1);
  not not_7 (not_7_out, Compare_0);
  not not_8 (not_8_out, Branch_1);
  not not_9 (not_9_out, Compare_2);
  not not_10 (not_10_out, Compare_0);
  not not_11 (not_11_out, Compare_1);
  not not_12 (not_12_out, Compare_0);
  and and_1 (and_1_out, Branch_2, not_1_out, not_2_out, not_3_out, Compare_0);
  and and_2 (and_2_out, Branch_2, not_4_out, not_5_out, Compare_2, not_6_out, not_7_out);
  and and_3 (and_3_out, Branch_2, not_8_out, Branch_0, not_9_out, Compare_1, not_10_out);
  and and_4 (and_4_out, Branch_2, Branch_1, Branch_0, Compare_2, not_11_out, not_12_out);
  or or_1 (change_PC_to_imm, and_1_out, and_2_out, and_3_out, and_4_out);
endmodule

module JR_Logic (
  input  Opcode_3,
  input  Opcode_2,
  input  Opcode_1,
  input  Opcode_0,
  input  Subop,
  output pc_to_rs
);

  wire not_1_out, not_2_out, not_3_out;

  not not_1 (not_1_out, Opcode_2);
  not not_2 (not_2_out, Opcode_1);
  not not_3 (not_3_out, Subop);
  and and_1 (pc_to_rs, Opcode_3, not_1_out, not_2_out, Opcode_0, not_3_out);
endmodule

module J_Logic (
  input  Opcode_3,
  input  Opcode_2,
  input  Opcode_1,
  input  Opcode_0,
  input  Subop,
  output pc_to_rs
);

  wire not_1_out;

  not not_1 (not_1_out, Opcode_1);
  and and_1 (pc_to_rs, Opcode_3, Opcode_2, not_1_out, Opcode_0);
endmodule

module JAL_Logic (
  input  Opcode_3,
  input  Opcode_2,
  input  Opcode_1,
  input  Opcode_0,
  input  Subop,
  output pc_to_rs
);

  wire not_1_out, not_2_out;

  not not_1 (not_1_out, Opcode_2);
  not not_2 (not_2_out, Opcode_1);
  and and_1 (pc_to_rs, Opcode_3, not_1_out, not_2_out, Opcode_0, Subop);
endmodule

module Write_Control (
  input  Opcode_3,
  input  Opcode_2,
  input  Opcode_1,
  input  Opcode_0,
  input  Subop,
  output Write
);

  wire and_1_out, and_2_out, and_3_out, and_4_out, and_5_out, not_1_out, not_2_out, not_3_out, not_4_out,
       not_5_out, not_6_out, not_7_out, not_8_out, not_9_out, not_10_out, not_11_out;

  not not_1 (not_1_out, Opcode_3);
  not not_2 (not_2_out, Opcode_2);
  not not_3 (not_3_out, Opcode_0);
  not not_4 (not_4_out, Opcode_3);
  not not_5 (not_5_out, Opcode_1);
  not not_6 (not_6_out, Opcode_3);
  not not_7 (not_7_out, Opcode_0);
  not not_8 (not_8_out, Subop);
  not not_9 (not_9_out, Opcode_2);
  not not_10 (not_10_out, Opcode_2);
  not not_11 (not_11_out, Subop);
  and and_1 (and_1_out, not_1_out, not_2_out, not_3_out);
  and and_2 (and_2_out, not_4_out, not_5_out);
  and and_3 (and_3_out, not_6_out, not_7_out, not_8_out);
  and and_4 (and_4_out, Opcode_3, not_9_out, Opcode_0, Subop);
  and and_5 (and_5_out, Opcode_3, not_10_out, Opcode_1, not_11_out);
  or or_1 (Write, and_1_out, and_2_out, and_3_out, and_4_out, and_5_out);
endmodule
